# Fritzing sketch MONITORING AIR (saved by Fritzing 0.9.3b)
breadboards: 1

parts:
  Part1 = Arduino Mega 2560 (Rev3)
  S1 = PH meter [package=THT]
  IC1 = DIP - 6 pins [chip_label="TDS METER V 1.0" package="DIP (Dual Inline) [THT]"]
  A1 = 2 channel relay module [package=THT]
  WATER_PUMP1 = water pump/motor  # not connected
  JACK1 = 2.1mm DC Barrel Jack

nets:
  N1: Part1.A0, S1.pin1
  5V: Part1.A1, Part1.5V, S1.pin3, IC1.A, IC1.VCC, A1.pin_13
  GND: Part1.GND, S1.pin2, IC1.GND, A1.pin_14
  N2: Part1.D5_PWM, A1.pin_16
  N3: Part1.D7_PWM, A1.pin_15
  N4: A1.pin_2, JACK1.sleeve

notes:
  220 v pln/ teganagn yang cocok untuk pompa
  Normal Close
  TSD METER
  PH
  vcc : vcc
  GND : GND
  A : A0
  IN : A0
  GND : GND
  VCC : VCC

custom parts:
  DIP - 6 pins: A DIP stand-in part for whatever IC you want. With 6 pins on a 300mil dual inline package (DIP) footprint.
  2 channel relay module: 2 channel Relay Module 5V 12V 24V High and Low Level Trigger Relay Control With Optocoupler Two Way relays DC 5 V 12 V 24 V Volt.
  water pump/motor: WATER PUMP BY ARDUBLOCKTR
  2.1mm DC Barrel Jack: 2.1mm DC Barrel Jack with Thru-Hole Connectors (breadboardable)
