# Fritzing sketch module Pengaduk (saved by Fritzing 0.9.3b)
breadboards: 1

parts:
  Part1 = Arduino Mega 2560 (Rev3)
  S1 = PH meter [package=THT]
  IC1 = DIP - 6 pins [chip_label="TDS METER V 1.0" package="DIP (Dual Inline) [THT]"]
  A1 = 2 channel relay module [package=THT]
  WATER_PUMP1 = water pump/motor  # not connected
  JACK1 = 2.1mm DC Barrel Jack
  OLED_I2C1 = OLED 128x64 I2C Monochrome Display
  WATER_PUMP2 = water pump/motor  # not connected
  YF-S201_Flow_Meter2 = YF-S201 Water Flow Meter
  A2 = 2 channel relay module [package=THT]
  YF-S201_Flow_Meter3 = YF-S201 Water Flow Meter
  YF-S201_Flow_Meter4 = YF-S201 Water Flow Meter
  YF-S201_Flow_Meter5 = YF-S201 Water Flow Meter
  J1 = Basic Servo
  J2 = Basic Servo
  J3 = Basic Servo
  J4 = Basic Servo
  M2 = JSN-SRO4T [package=THT]

nets:
  N1: Part1.A0, S1.pin1
  VCC: Part1.A1, Part1.5V, S1.pin3, IC1.A, IC1.VCC, A1.pin_13, OLED_I2C1.VDD, YF-S201_Flow_Meter2.VCC, A2.pin_13, YF-S201_Flow_Meter5.VCC
  N2: Part1.A2, J1.pulse
  N3: Part1.A3, J4.pulse
  N4: Part1.A5, J2.pulse
  N5: Part1.A6, J3.pulse
  N6: Part1.D21/SCL, OLED_I2C1.SDA
  N7: Part1.D20/SDA, OLED_I2C1.SCK
  N8: Part1.D15/RX3, M2.pin3
  N9: Part1.D14/TX3, M2.pin2
  GND: Part1.GND, S1.pin2, IC1.GND, A1.pin_14, OLED_I2C1.GND, YF-S201_Flow_Meter2.GND, A2.pin_14, YF-S201_Flow_Meter5.GND
  N10: Part1.D0_RX0, A2.pin_15
  N11: Part1.D1_TX0, YF-S201_Flow_Meter4.SIG
  N12: Part1.D2_PWM, YF-S201_Flow_Meter5.SIG
  N13: Part1.D3_PWM, YF-S201_Flow_Meter3.SIG
  N14: Part1.D4_PWM, YF-S201_Flow_Meter2.SIG
  N15: Part1.D5_PWM, A1.pin_16
  N16: Part1.D7_PWM, A1.pin_15
  N17: A1.pin_1, JACK1.sleeve
  N18: A1.pin_3, A1.pin_4

notes:
  220 v pln/ teganagn yang cocok untuk pompa
  Normal Close
  TSD METER
  PH
  vcc : vcc
  GND : GND
  A : A0
  IN : A0
  GND : GND
  VCC : VCC
  SDA : SDA
  SCL : SCL
  GND : GND
  VCC : VCC
  SOCKET KE TDS
  SOCKET KE PH SENSOR
  INPUT 1 KE INPUT 2
  GND : GND
  VCC : VCC
  PIN : A2
  GND : GND
  VCC : VCC
  PIN : A3
  GND : GND
  VCC : VCC
  PIN : A6
  GND : GND
  VCC : VCC
  PIN : A5
  GND : GND
  VCC : VCC
  PIN : D4
  GND : GND
  VCC : VCC
  PIN : D3
  GND : GND
  VCC : VCC
  PIN : D2
  GND : GND
  VCC : VCC
  PIN : D6
  KE PENGADUK
  VCC : VCC
  GND : GND
  TRIG : D15
  ECHO : 14

custom parts:
  DIP - 6 pins: A DIP stand-in part for whatever IC you want. With 6 pins on a 300mil dual inline package (DIP) footprint.
  2 channel relay module: 2 channel Relay Module 5V 12V 24V High and Low Level Trigger Relay Control With Optocoupler Two Way relays DC 5 V 12 V 24 V Volt.
  water pump/motor: WATER PUMP BY ARDUBLOCKTR
  2.1mm DC Barrel Jack: 2.1mm DC Barrel Jack with Thru-Hole Connectors (breadboardable)
  YF-S201 Water Flow Meter: The YF-S201 Flow Meter. The input voltage is 5V to 24V (DC).
  JSN-SRO4T: JSN-SR04T Waterproof Ultrasonic Distance Measuring Module Integrated Ultrasonic Detection Module DC 5V.
